// Logisim project Relogio completo.circ as structural Verilog: 6 circuits, main circuit contador0a9
module relogioDigital (
  input  in_1,
  input  in_2,
  input  up_down,
  output [3:0] out_4,
  output [3:0] out_5,
  output [3:0] out_6,
  output [3:0] out_7,
  output [3:0] out_8,
  output [3:0] out_9
);

  wire and_1_out, and_2_out, and_3_out, and_4_out, and_5_out, and_6_out, and_7_out, and_8_out, and_9_out,
       and_10_out, and_11_out, and_12_out, and_13_out, and_14_out, and_15_out, and_16_out, and_17_out,
       and_18_out, and_19_out, and_20_out, and_21_out, and_22_out, and_23_out, and_24_out, and_25_out,
       and_26_out, and_27_out, and_28_out, and_29_out, and_30_out, and_31_out, and_32_out, and_33_out,
       and_34_out, and_35_out, and_36_out, and_37_out, circuito_display_1_a, circuito_display_1_b,
       circuito_display_1_c, circuito_display_1_d, circuito_display_1_e, circuito_display_1_f,
       circuito_display_1_g, circuito_display_2_a, circuito_display_2_b, circuito_display_2_c,
       circuito_display_2_d, circuito_display_2_e, circuito_display_2_f, circuito_display_2_g,
       circuito_display_3_a, circuito_display_3_b, circuito_display_3_c, circuito_display_3_d,
       circuito_display_3_e, circuito_display_3_f, circuito_display_3_g, circuito_display_4_a,
       circuito_display_4_b, circuito_display_4_c, circuito_display_4_d, circuito_display_4_e,
       circuito_display_4_f, circuito_display_4_g, circuito_display_5_a, circuito_display_5_b,
       circuito_display_5_c, circuito_display_5_d, circuito_display_5_e, circuito_display_5_f,
       circuito_display_5_g, circuito_display_6_a, circuito_display_6_b, circuito_display_6_c,
       circuito_display_6_d, circuito_display_6_e, circuito_display_6_f, circuito_display_6_g, clock_1_out,
       contador0a5_1_d0, contador0a5_1_d1, contador0a5_1_out_4, contador0a5_2_d0, contador0a5_2_d1,
       contador0a5_2_out_4, contador0a5_3_d0, contador0a5_3_d1, contador0a5_3_out_4, contador0a9_1_d0,
       contador0a9_1_d1, contador0a9_1_d3, contador0a9_1_out_6, contador0a9_2_d0, contador0a9_2_d1,
       contador0a9_2_d3, contador0a9_2_out_6, contador0a9_3_d0, contador0a9_3_d1, contador0a9_3_d3,
       contador0a9_3_out_6, contador5a0_d1, contador5a0_out_4, contador9a0_1_d1, contador9a0_1_d2,
       contador9a0_2_d0, contador9a0_2_d1, contador9a0_2_d2, contador9a0_2_d3, d_ff_1_q, d_ff_3_q, d_ff_6_q,
       d_ff_12_q, d_ff_15_q, d_ff_16_q, nand_1_out, nand_2_out, nand_3_out, nor_1_out, not_1_out, not_2_out,
       not_3_out, not_4_out, not_5_out, not_6_out, not_7_out, not_8_out, not_9_out, not_10_out, not_11_out,
       not_12_out, not_13_out, not_14_out, not_15_out, not_16_out, not_17_out, not_18_out, not_19_out,
       not_20_out, not_21_out, not_22_out, not_23_out, not_24_out, not_25_out, not_26_out, not_27_out,
       not_28_out, or_1_out, or_2_out, or_3_out, or_4_out, or_5_out, or_6_out, or_7_out, or_8_out, or_9_out,
       relog_23_59_59_out, xor_1_out, xor_2_out, xor_3_out, xor_4_out, xor_5_out;
  wire [2:0] d_ff_5_q, d_ff_14_q, Q0_q;
  wire [3:0] d_ff_10_q;

  not not_1 (not_1_out, and_4_out);
  and and_1 (and_1_out, and_3_out, not_1_out);
  not not_2 (not_2_out, and_5_out);
  and and_2 (and_2_out, d_ff_5_q[1], not_3_out);
  not not_3 (not_3_out, d_ff_5_q[0]);
  circuito_display circuito_display_1 (
    .D3(1'b0), .D2(d_ff_5_q[2]), .D1(d_ff_5_q[1]), .D0(d_ff_5_q[0]), .a(circuito_display_1_a),
    .b(circuito_display_1_b), .c(circuito_display_1_c), .d(circuito_display_1_d), .e(circuito_display_1_e),
    .f(circuito_display_1_f), .g(circuito_display_1_g));
  D_Flip_Flop d_ff_1 (.clk(xor_2_out), .D(and_5_out), .Q(d_ff_1_q));  // open: Qn, preset, en, reset
  _7_Segment_Display u_7_segment_display_1 (
    .g(circuito_display_1_g), .f(circuito_display_1_f), .a(circuito_display_1_a), .b(circuito_display_1_b),
    .e(circuito_display_1_e), .d(circuito_display_1_d), .c(circuito_display_1_c));  // open: dp
  LED led_1 (.in(and_4_out));
  and and_3 (and_3_out, not_2_out, d_ff_1_q);
  D_Flip_Flop d_ff_2 (
    .clk(and_1_out), .D(contador0a5_1_out_4), .Q(d_ff_5_q[2]), .reset(xor_1_out));  // open: Qn, preset, en
  and and_4 (and_4_out, and_8_out, and_2_out);
  not not_4 (not_4_out, d_ff_5_q[1]);
  D_Flip_Flop d_ff_3 (.clk(clock_1_out), .D(relog_23_59_59_out), .Q(d_ff_3_q));  // open: Qn, preset, en, reset
  LED led_2 (.in(relog_23_59_59_out));
  and and_5 (and_5_out, and_9_out, not_4_out);
  D_Flip_Flop d_ff_4 (
    .clk(and_1_out), .D(contador0a5_1_d1), .Q(d_ff_5_q[1]), .reset(xor_1_out));  // open: Qn, preset, en
  nand nand_1 (nand_1_out, d_ff_5_q[0], d_ff_5_q[1]);
  and relog_23_59_59 (relog_23_59_59_out, and_10_out, and_4_out);
  not not_5 (not_5_out, d_ff_10_q[2]);
  not not_6 (not_6_out, d_ff_10_q[3]);
  not not_7 (not_7_out, d_ff_10_q[1]);
  not not_8 (not_8_out, d_ff_10_q[2]);
  D_Flip_Flop d_ff_5 (
    .clk(and_1_out), .D(contador0a5_1_d0), .Q(d_ff_5_q[0]), .reset(xor_1_out));  // open: Qn, preset, en
  not not_9 (not_9_out, nand_1_out);
  and and_6 (and_6_out, relog_23_59_59_out, d_ff_3_q);
  and and_7 (and_7_out, d_ff_3_q, clock_1_out);
  and and_8 (and_8_out, d_ff_10_q[0], d_ff_10_q[1], not_5_out, not_6_out);
  and and_9 (and_9_out, d_ff_10_q[0], not_7_out, not_8_out, d_ff_10_q[3]);
  contador0a5 contador0a5_1 (
    .Q2(d_ff_5_q[2]), .Q1(d_ff_5_q[1]), .Q0(d_ff_5_q[0]), .out_4(contador0a5_1_out_4), .D1(contador0a5_1_d1),
    .D0(contador0a5_1_d0));
  xor xor_1 (xor_1_out, not_9_out, and_6_out);
  D_Flip_Flop d_ff_6 (.clk(xor_3_out), .D(and_12_out), .Q(d_ff_6_q));  // open: Qn, preset, en, reset
  circuito_display circuito_display_2 (
    .D3(d_ff_10_q[3]), .D2(d_ff_10_q[2]), .D1(d_ff_10_q[1]), .D0(d_ff_10_q[0]), .a(circuito_display_2_a),
    .b(circuito_display_2_b), .c(circuito_display_2_c), .d(circuito_display_2_d), .e(circuito_display_2_e),
    .f(circuito_display_2_f), .g(circuito_display_2_g));
  _7_Segment_Display u_7_segment_display_2 (
    .g(circuito_display_2_g), .f(circuito_display_2_f), .a(circuito_display_2_a), .b(circuito_display_2_b),
    .e(circuito_display_2_e), .d(circuito_display_2_d), .c(circuito_display_2_c));  // open: dp
  D_Flip_Flop d_ff_7 (
    .clk(xor_2_out), .D(contador0a9_1_d3), .Q(d_ff_10_q[3]), .Qn(out_8[3]), .reset(and_7_out));  // open: preset, en
  Hex_Digit_Display hex_digit_display_1 (.value({1'b0, d_ff_5_q}));  // open: dp
  xor xor_2 (xor_2_out, d_ff_6_q, and_12_out);
  D_Flip_Flop d_ff_8 (
    .clk(xor_2_out), .D(contador0a9_1_out_6), .Q(d_ff_10_q[2]), .Qn(out_8[2]), .reset(and_7_out));  // open: preset, en
  Hex_Digit_Display hex_digit_display_2 (.value(d_ff_10_q));  // open: dp
  Hex_Digit_Display hex_digit_display_3 (.value({1'b0, d_ff_14_q}));  // open: dp
  not not_10 (not_10_out, 1'b0);
  not not_11 (not_11_out, 1'b0);
  D_Flip_Flop d_ff_9 (
    .clk(xor_2_out), .D(contador0a9_1_d1), .Q(d_ff_10_q[1]), .Qn(out_8[1]), .reset(and_7_out));  // open: preset, en
  Hex_Digit_Display hex_digit_display_4 (.value(out_4));  // open: dp
  and and_10 (and_10_out, and_22_out, and_13_out);
  not not_12 (not_12_out, d_ff_14_q[1]);
  not not_13 (not_13_out, 1'b0);
  D_Flip_Flop d_ff_10 (
    .clk(xor_2_out), .D(contador0a9_1_d0), .Q(d_ff_10_q[0]), .Qn(out_8[0]), .reset(and_7_out));  // open: preset, en
  Hex_Digit_Display hex_digit_display_5 (.value({1'b0, Q0_q}));  // open: dp
  and and_11 (and_11_out, not_12_out, not_13_out, d_ff_14_q[2], d_ff_14_q[0]);
  and and_12 (and_12_out, not_10_out, d_ff_14_q[1], d_ff_14_q[2], not_11_out);
  contador0a9 contador0a9_1 (
    .Q3(d_ff_10_q[3]), .Q2(d_ff_10_q[2]), .Q1(d_ff_10_q[1]), .Q0(d_ff_10_q[0]), .D3(contador0a9_1_d3),
    .out_6(contador0a9_1_out_6), .D1(contador0a9_1_d1), .D0(contador0a9_1_d0));
  Hex_Digit_Display hex_digit_display_6 (.value(out_6));  // open: dp
  circuito_display circuito_display_3 (
    .D3(1'b0), .D2(d_ff_14_q[2]), .D1(d_ff_14_q[1]), .D0(d_ff_14_q[0]), .a(circuito_display_3_a),
    .b(circuito_display_3_b), .c(circuito_display_3_c), .d(circuito_display_3_d), .e(circuito_display_3_e),
    .f(circuito_display_3_f), .g(circuito_display_3_g));
  and and_13 (and_13_out, and_11_out, and_15_out);
  _7_Segment_Display u_7_segment_display_3 (
    .g(circuito_display_3_g), .f(circuito_display_3_f), .a(circuito_display_3_a), .b(circuito_display_3_b),
    .e(circuito_display_3_e), .d(circuito_display_3_d), .c(circuito_display_3_c));  // open: dp
  D_Flip_Flop d_ff_11 (
    .clk(and_14_out), .D(contador0a5_2_out_4), .Q(d_ff_14_q[2]), .reset(not_17_out));  // open: Qn, preset, en
  D_Flip_Flop d_ff_12 (.clk(xor_3_out), .D(and_15_out), .Q(d_ff_12_q));  // open: Qn, preset, en, reset
  D_Flip_Flop d_ff_13 (
    .clk(and_14_out), .D(contador0a5_2_d1), .Q(d_ff_14_q[1]), .reset(not_17_out));  // open: Qn, preset, en
  not not_14 (not_14_out, and_15_out);
  not not_15 (not_15_out, out_4[1]);
  not not_16 (not_16_out, out_4[2]);
  not not_17 (not_17_out, nand_2_out);
  nand nand_2 (nand_2_out, d_ff_14_q[2], d_ff_14_q[1]);
  and and_14 (and_14_out, d_ff_12_q, not_14_out);
  and and_15 (and_15_out, out_4[0], not_15_out, not_16_out, out_4[3]);
  contador0a5 contador0a5_2 (
    .Q2(d_ff_14_q[2]), .Q1(d_ff_14_q[1]), .Q0(d_ff_14_q[0]), .out_4(contador0a5_2_out_4),
    .D1(contador0a5_2_d1), .D0(contador0a5_2_d0));
  D_Flip_Flop d_ff_14 (
    .clk(and_14_out), .D(contador0a5_2_d0), .Q(d_ff_14_q[0]), .reset(not_17_out));  // open: Qn, preset, en
  not not_18 (not_18_out, up_down);
  and and_16 (and_16_out, contador0a9_2_d1, not_18_out);
  and and_17 (and_17_out, contador9a0_1_d1, up_down);
  xor xor_3 (xor_3_out, d_ff_15_q, and_21_out);
  D_Flip_Flop D3 (
    .clk(xor_3_out), .D(contador0a9_2_d3), .Q(out_4[3]), .Qn(out_7[3]), .reset(in_1));  // open: preset, en
  or or_1 (or_1_out, and_16_out, and_17_out);
  D_Flip_Flop D2 (
    .clk(xor_3_out), .D(contador0a9_2_out_6), .Q(out_4[2]), .Qn(out_7[2]), .reset(in_1));  // open: preset, en
  D_Flip_Flop d_ff_15 (.clk(clock_1_out), .D(and_21_out), .Q(d_ff_15_q));  // open: Qn, preset, en, reset
  circuito_display circuito_display_4 (
    .D3(out_4[3]), .D2(out_4[2]), .D1(out_4[1]), .D0(out_4[0]), .a(circuito_display_4_a),
    .b(circuito_display_4_b), .c(circuito_display_4_c), .d(circuito_display_4_d), .e(circuito_display_4_e),
    .f(circuito_display_4_f), .g(circuito_display_4_g));
  and and_18 (and_18_out, contador0a9_2_out_6, not_18_out);
  or or_2 (or_2_out, and_18_out, and_19_out);
  and and_19 (and_19_out, contador9a0_1_d2, up_down);
  _7_Segment_Display u_7_segment_display_4 (
    .g(circuito_display_4_g), .f(circuito_display_4_f), .a(circuito_display_4_a), .b(circuito_display_4_b),
    .e(circuito_display_4_e), .d(circuito_display_4_d), .c(circuito_display_4_c));  // open: dp
  D_Flip_Flop D1 (.clk(xor_3_out), .D(or_1_out), .Q(out_4[1]), .Qn(out_7[1]), .reset(in_1));  // open: preset, en
  not not_19 (not_19_out, 1'b0);
  not not_20 (not_20_out, Q0_q[1]);
  D_Flip_Flop D0 (
    .clk(xor_3_out), .D(contador0a9_2_d0), .Q(out_4[0]), .Qn(out_7[0]), .reset(in_1));  // open: preset, en
  and and_20 (and_20_out, not_19_out, Q0_q[0], not_20_out, Q0_q[2]);
  not not_21 (not_21_out, 1'b0);
  contador9a0 contador9a0_1 (
    .Q3(contador0a9_2_d3), .Q2(contador0a9_2_out_6), .Q1(contador0a9_2_d1), .Q0(contador0a9_2_d0),
    .D2(contador9a0_1_d2), .D1(contador9a0_1_d1));  // open: D3, D0
  not not_22 (not_22_out, Q0_q[0]);
  and and_21 (and_21_out, Q0_q[1], not_22_out, Q0_q[2], not_21_out);
  contador0a9 contador0a9_2 (
    .Q3(out_4[3]), .Q2(out_4[2]), .Q1(out_4[1]), .Q0(out_4[0]), .D3(contador0a9_2_d3),
    .out_6(contador0a9_2_out_6), .D1(contador0a9_2_d1), .D0(contador0a9_2_d0));
  and and_22 (and_22_out, and_29_out, and_20_out);
  LED led_3 (.in(and_22_out));
  D_Flip_Flop Q2 (.clk(xor_5_out), .D(or_3_out), .Q(Q0_q[2]), .reset(not_24_out));  // open: Qn, preset, en
  contador5a0 contador5a0 (
    .Q2(Q0_q[2]), .Q1(Q0_q[1]), .Q0(Q0_q[0]), .out_4(contador5a0_out_4), .D1(contador5a0_d1));  // open: D0
  circuito_display circuito_display_5 (
    .D3(1'b0), .D2(Q0_q[2]), .D1(Q0_q[1]), .D0(Q0_q[0]), .a(circuito_display_5_a), .b(circuito_display_5_b),
    .c(circuito_display_5_c), .d(circuito_display_5_d), .e(circuito_display_5_e), .f(circuito_display_5_f),
    .g(circuito_display_5_g));
  not not_23 (not_23_out, up_down);
  _7_Segment_Display u_7_segment_display_5 (
    .g(circuito_display_5_g), .f(circuito_display_5_f), .a(circuito_display_5_a), .b(circuito_display_5_b),
    .e(circuito_display_5_e), .d(circuito_display_5_d), .c(circuito_display_5_c));  // open: dp
  and and_23 (and_23_out, contador0a5_3_out_4, not_23_out);
  and and_24 (and_24_out, contador5a0_out_4, up_down);
  and and_25 (and_25_out, contador0a5_3_d1, not_23_out);
  and and_26 (and_26_out, contador5a0_d1, up_down);
  D_Flip_Flop Q1 (.clk(xor_5_out), .D(or_4_out), .Q(Q0_q[1]), .reset(not_24_out));  // open: Qn, preset, en
  nand nand_3 (nand_3_out, Q0_q[2], Q0_q[1]);
  or or_3 (or_3_out, and_23_out, and_24_out);
  or or_4 (or_4_out, and_25_out, and_26_out);
  D_Flip_Flop Q0 (.clk(xor_5_out), .D(contador0a5_3_d0), .Q(Q0_q[0]), .reset(not_24_out));  // open: Qn, preset, en
  not not_24 (not_24_out, nand_3_out);
  LED led_4 (.in(or_4_out));
  contador0a5 contador0a5_3 (
    .Q2(Q0_q[2]), .Q1(Q0_q[1]), .Q0(Q0_q[0]), .out_4(contador0a5_3_out_4), .D1(contador0a5_3_d1),
    .D0(contador0a5_3_d0));
  LED led_5 (.in(and_29_out));
  LED led_6 (.in(nor_1_out));
  LED led_7 (.in(Q0_q[0]));
  not not_25 (not_25_out, or_5_out);
  and and_27 (and_27_out, and_29_out, not_23_out);
  and and_28 (and_28_out, up_down, nor_1_out);
  nor nor_1 (nor_1_out, and_29_out, out_6[3], out_6[1], out_6[0]);
  LED led_8 (.in(or_5_out));
  or or_5 (or_5_out, and_27_out, and_28_out);
  D_Flip_Flop d_ff_16 (.clk(and_29_out), .D(and_29_out), .Q(d_ff_16_q));  // open: Qn, preset, en, reset
  Clock clock_1 (.out(clock_1_out));
  D_Flip_Flop D3_2 (.clk(clock_1_out), .D(or_6_out), .Q(out_6[3]), .Qn(out_9[3]), .reset(in_2));  // open: preset, en
  LED led_9 (.in(xor_5_out));
  xor xor_4 (xor_4_out, d_ff_16_q, and_29_out);
  D_Flip_Flop D2_2 (.clk(clock_1_out), .D(or_7_out), .Q(out_6[2]), .Qn(out_9[2]), .reset(in_2));  // open: preset, en
  xor xor_5 (xor_5_out, xor_4_out, up_down);
  LED led_10 (.in(or_8_out));
  D_Flip_Flop D1_2 (.clk(clock_1_out), .D(or_8_out), .Q(out_6[1]), .Qn(out_9[1]), .reset(in_2));  // open: preset, en
  not not_26 (not_26_out, out_6[1]);
  not not_27 (not_27_out, out_6[2]);
  D_Flip_Flop D0_2 (
    .clk(clock_1_out), .D(contador0a9_3_d0), .Q(out_6[0]), .Qn(out_9[0]), .reset(in_2));  // open: preset, en
  and and_29 (and_29_out, out_6[0], not_26_out, not_27_out, out_6[3]);
  LED led_11 (.in(contador0a9_3_out_6));
  circuito_display circuito_display_6 (
    .D3(out_6[3]), .D2(out_6[2]), .D1(out_6[1]), .D0(out_6[0]), .a(circuito_display_6_a),
    .b(circuito_display_6_b), .c(circuito_display_6_c), .d(circuito_display_6_d), .e(circuito_display_6_e),
    .f(circuito_display_6_f), .g(circuito_display_6_g));
  contador9a0 contador9a0_2 (
    .Q3(out_6[3]), .Q2(out_6[2]), .Q1(out_6[1]), .Q0(out_6[0]), .D3(contador9a0_2_d3), .D2(contador9a0_2_d2),
    .D1(contador9a0_2_d1), .D0(contador9a0_2_d0));
  contador0a9 contador0a9_3 (
    .Q3(out_6[3]), .Q2(out_6[2]), .Q1(out_6[1]), .Q0(out_6[0]), .D3(contador0a9_3_d3),
    .out_6(contador0a9_3_out_6), .D1(contador0a9_3_d1), .D0(contador0a9_3_d0));
  _7_Segment_Display u_7_segment_display_6 (
    .g(circuito_display_6_g), .f(circuito_display_6_f), .a(circuito_display_6_a), .b(circuito_display_6_b),
    .e(circuito_display_6_e), .d(circuito_display_6_d), .c(circuito_display_6_c));  // open: dp
  not not_28 (not_28_out, up_down);
  LED led_12 (.in(up_down));
  LED led_13 (.in(and_30_out));
  and and_30 (and_30_out, contador0a9_3_d3, not_28_out);
  and and_31 (and_31_out, contador9a0_2_d3, up_down);
  and and_32 (and_32_out, contador0a9_3_out_6, not_28_out);
  and and_33 (and_33_out, contador9a0_2_d2, up_down);
  LED led_14 (.in(and_34_out));
  and and_34 (and_34_out, not_28_out, contador0a9_3_d1);
  and and_35 (and_35_out, up_down, contador9a0_2_d1);
  LED led_15 (.in(and_35_out));
  and and_36 (and_36_out, not_28_out, contador0a9_3_d0);
  and and_37 (and_37_out, up_down, contador9a0_2_d0);
  or or_6 (or_6_out, and_30_out, and_31_out);
  LED led_16 (.in(and_31_out));
  LED led_17 (.in(and_32_out));
  or or_7 (or_7_out, and_32_out, and_33_out);
  LED led_18 (.in(and_33_out));
  or or_8 (or_8_out, and_34_out, and_35_out);
  or or_9 (or_9_out, and_36_out, and_37_out);
  LED led_19 (.in(or_6_out));
  LED led_20 (.in(or_7_out));
  LED led_21 (.in(or_8_out));
  LED led_22 (.in(or_9_out));

  // Notes on the sheet:
  //   Contador de 0 a 2, para horas
  //   dezena = 2
  //   identifica o 09 e 19
  //   Contador de 0 a 9, para unidade de minutos e segundos
  //   hora = 23
  //   identifica o 23 na hora
  //   unidade = 3
  //   identifica o 9
  //   Contador de 0 a 5, para dezenas de minutos e segundos
  //   identifica o 5  na dezena de minutos
  //   identifica o 9 na unidade de minutos
  //   identifica o 5 na dezena do seg
  //   identifica 0 9 na unidade de segundos
endmodule

module contador0a9 (
  input  Q3,
  input  Q2,
  input  Q1,
  input  Q0,
  output D3,
  output out_6,
  output D1,
  output D0
);

  wire and_1_out, and_2_out, and_3_out, and_4_out, and_5_out, and_6_out, and_7_out, not_1_out, not_2_out,
       not_3_out, not_4_out, not_5_out, not_6_out, not_7_out, not_8_out;

  not not_1 (not_1_out, Q1);
  not not_2 (not_2_out, Q0);
  not not_3 (not_3_out, Q0);
  not not_4 (not_4_out, Q2);
  not not_5 (not_5_out, Q1);
  not not_6 (not_6_out, Q1);
  not not_7 (not_7_out, Q3);
  not not_8 (not_8_out, Q0);
  and and_1 (and_1_out, Q2, Q1, Q0);
  and and_2 (and_2_out, not_1_out, Q3, not_2_out);
  and and_3 (and_3_out, Q2, Q1, not_3_out);
  and and_4 (and_4_out, Q0, Q1, not_4_out);
  and and_5 (and_5_out, Q2, not_5_out);
  and and_6 (and_6_out, not_6_out, Q0, not_7_out);
  and and_7 (and_7_out, Q1, not_8_out);
  or or_1 (D3, and_1_out, and_2_out);
  or or_2 (out_6, and_3_out, and_4_out, and_5_out);
  or or_3 (D1, and_6_out, and_7_out);
  not not_9 (D0, Q0);

  // Notes on the sheet:
  //   CONTADOR DE 0 A 9
endmodule

module contador0a5 (
  input  Q2,
  input  Q1,
  input  Q0,
  output out_4,
  output D1,
  output D0
);

  wire and_1_out, and_2_out, and_3_out, and_4_out, and_5_out, not_1_out, not_2_out, not_3_out, not_4_out,
       not_5_out;

  not not_1 (not_1_out, Q0);
  not not_2 (not_2_out, Q2);
  not not_3 (not_3_out, Q1);
  not not_4 (not_4_out, Q1);
  not not_5 (not_5_out, Q0);
  and and_1 (and_1_out, Q2, Q1, not_1_out);
  and and_2 (and_2_out, Q0, Q1, not_2_out);
  and and_3 (and_3_out, Q2, not_3_out);
  and and_4 (and_4_out, not_4_out, Q0);
  and and_5 (and_5_out, Q1, not_5_out);
  or or_1 (out_4, and_1_out, and_2_out, and_3_out);
  or or_2 (D1, and_4_out, and_5_out);
  not not_6 (D0, Q0);
endmodule

module circuito_display (
  input  D3,
  input  D2,
  input  D1,
  input  D0,
  output a,
  output b,
  output c,
  output d,
  output e,
  output f,
  output g
);

  wire nand_1_out, nand_2_out, nand_3_out, nand_4_out, nand_5_out, nand_6_out, nand_7_out, nand_8_out,
       nand_9_out, nand_10_out, nand_11_out, nand_12_out, nand_13_out, nand_14_out, nand_15_out, nand_16_out,
       nand_17_out, nand_18_out, nand_19_out, nand_20_out, nand_21_out, nand_22_out, nand_23_out,
       nand_24_out, nand_25_out, nand_26_out, nand_27_out, nand_28_out, nand_29_out, nand_30_out,
       nand_31_out, nand_32_out, nand_33_out, nand_34_out, nand_35_out, nand_36_out, nand_37_out,
       nand_38_out, nand_39_out, nand_40_out, nand_41_out, nand_42_out, nand_43_out, nand_44_out,
       nand_45_out, nand_46_out, nand_47_out, nand_48_out, nand_49_out, nand_50_out, nand_51_out,
       nand_52_out, nand_53_out, nand_54_out, nand_55_out, nand_56_out, nand_57_out, nand_58_out,
       nand_59_out, nand_60_out, nand_61_out, nand_62_out, nand_63_out, nand_64_out, nand_65_out,
       nand_66_out, nand_67_out, nand_68_out, nand_69_out, nand_70_out, nand_71_out, nand_72_out,
       nand_73_out, nand_74_out, nand_75_out, nand_76_out, nand_77_out, nand_78_out, nand_79_out,
       nand_80_out, nand_81_out, nand_83_out, nand_84_out, nand_85_out, nand_86_out, nand_87_out,
       nand_88_out, nand_89_out, nand_90_out, nand_91_out, nand_92_out, nand_93_out, nand_94_out,
       nand_95_out, nand_96_out, nand_97_out, nand_98_out, nand_99_out, nand_100_out, nand_101_out,
       nand_102_out, nand_103_out, nand_104_out, nand_105_out, nand_106_out, nand_107_out, nand_108_out,
       nand_109_out, nand_110_out, nand_111_out, nand_112_out, nand_113_out, nand_114_out, nand_115_out,
       nand_116_out, nand_117_out, nand_118_out, nand_119_out, nand_120_out, nand_121_out, nand_122_out,
       nand_123_out, nand_124_out, nand_125_out, nand_126_out, nand_127_out, nand_128_out, nand_129_out,
       nand_130_out, nand_131_out, nand_132_out, nand_133_out, nand_134_out, nand_135_out, nand_136_out,
       nand_137_out, nand_138_out, nand_139_out, nand_141_out, nand_142_out, nand_143_out, nand_144_out,
       nand_146_out, nand_147_out, nand_148_out;

  nand nand_1 (nand_1_out, D2, D2);
  nand nand_2 (nand_2_out, D3, D3);
  nand nand_3 (nand_3_out, D1, D1);
  nand nand_4 (nand_4_out, D3, D3);
  nand nand_5 (nand_5_out, D1, D1);
  nand nand_6 (nand_6_out, D3, D3);
  nand nand_7 (nand_7_out, D3, D3);
  nand nand_8 (nand_8_out, D2, D2);
  nand nand_9 (nand_9_out, D2, D2);
  nand nand_10 (nand_10_out, D2, D2);
  nand nand_11 (nand_11_out, D0, D0);
  nand nand_12 (nand_12_out, D0, D0);
  nand nand_13 (nand_13_out, D3, D3);
  nand nand_14 (nand_14_out, D2, D2);
  nand nand_15 (nand_15_out, D0, D0);
  nand nand_16 (nand_16_out, D3, D3);
  nand nand_17 (nand_17_out, D2, D2);
  nand nand_18 (nand_18_out, D0, D0);
  nand nand_19 (nand_19_out, D3, D3);
  nand nand_20 (nand_20_out, D3, D3);
  nand nand_21 (nand_21_out, D3, nand_1_out);
  nand nand_22 (nand_22_out, D3, D3);
  nand nand_23 (nand_23_out, D2, D2);
  nand nand_24 (nand_24_out, nand_2_out, nand_3_out);
  nand nand_25 (nand_25_out, nand_4_out, nand_5_out);
  nand nand_26 (nand_26_out, nand_6_out, D0);
  nand nand_27 (nand_27_out, nand_7_out, nand_8_out);
  nand nand_28 (nand_28_out, nand_9_out, D1);
  nand nand_29 (nand_29_out, nand_10_out, nand_11_out);
  nand nand_30 (nand_30_out, D1, nand_12_out);
  nand nand_31 (nand_31_out, D3, D1);
  nand nand_32 (nand_32_out, D3, D2);
  nand nand_33 (nand_33_out, D1, D1);
  nand nand_34 (nand_34_out, D0, D0);
  nand nand_35 (nand_35_out, nand_13_out, D2);
  nand nand_36 (nand_36_out, nand_14_out, D1);
  nand nand_37 (nand_37_out, D1, nand_15_out);
  nand nand_38 (nand_38_out, nand_16_out, D2);
  nand nand_39 (nand_39_out, nand_17_out, nand_18_out);
  nand nand_40 (nand_40_out, nand_19_out, D1);
  nand nand_41 (nand_41_out, nand_20_out, D2);
  nand nand_42 (nand_42_out, nand_21_out, nand_21_out);
  nand nand_43 (nand_43_out, D1, D1);
  nand nand_44 (nand_44_out, nand_22_out, nand_23_out);
  nand nand_45 (nand_45_out, nand_24_out, nand_24_out);
  nand nand_46 (nand_46_out, D0, D0);
  nand nand_47 (nand_47_out, D3, D3);
  nand nand_48 (nand_48_out, D1, D1);
  nand nand_49 (nand_49_out, nand_25_out, nand_26_out);
  nand nand_50 (nand_50_out, nand_27_out, nand_27_out);
  nand nand_51 (nand_51_out, D0, D0);
  nand nand_52 (nand_52_out, nand_28_out, nand_28_out);
  nand nand_53 (nand_53_out, D1, D1);
  nand nand_54 (nand_54_out, D1, D1);
  nand nand_55 (nand_55_out, nand_29_out, nand_30_out);
  nand nand_56 (nand_56_out, nand_31_out, nand_32_out);
  nand nand_57 (nand_57_out, nand_33_out, nand_34_out);
  nand nand_58 (nand_58_out, nand_35_out, nand_35_out);
  nand nand_59 (nand_59_out, D1, D1);
  nand nand_60 (nand_60_out, nand_36_out, nand_37_out);
  nand nand_61 (nand_61_out, nand_38_out, nand_38_out);
  nand nand_62 (nand_62_out, D1, D1);
  nand nand_63 (nand_63_out, D2, D2);
  nand nand_64 (nand_64_out, nand_39_out, nand_40_out);
  nand nand_65 (nand_65_out, D2, D1);
  nand nand_66 (nand_66_out, nand_42_out, nand_43_out);
  nand nand_67 (nand_67_out, nand_45_out, nand_46_out);
  nand nand_68 (nand_68_out, D2, D2);
  nand nand_69 (nand_69_out, D0, D0);
  nand nand_70 (nand_70_out, nand_47_out, D1);
  nand nand_71 (nand_71_out, D3, nand_48_out);
  nand nand_72 (nand_72_out, nand_49_out, nand_49_out);
  nand nand_73 (nand_73_out, D1, D1);
  nand nand_74 (nand_74_out, D3, D3);
  nand nand_75 (nand_75_out, D2, D2);
  nand nand_76 (nand_76_out, nand_50_out, nand_51_out);
  nand nand_77 (nand_77_out, nand_52_out, D0);
  nand nand_78 (nand_78_out, D2, nand_53_out);
  nand nand_79 (nand_79_out, D2, D1);
  nand nand_80 (nand_80_out, D3, nand_54_out);
  nand nand_81 (nand_81_out, nand_55_out, nand_55_out);
  nand nand_82 (e, nand_81_out, nand_83_out);
  nand nand_83 (nand_83_out, nand_56_out, nand_56_out);
  nand nand_84 (nand_84_out, nand_58_out, nand_59_out);
  nand nand_85 (nand_85_out, nand_60_out, nand_60_out);
  nand nand_86 (nand_86_out, nand_61_out, nand_62_out);
  nand nand_87 (nand_87_out, D3, nand_63_out);
  nand nand_88 (nand_88_out, D3, D0);
  nand nand_89 (nand_89_out, nand_64_out, nand_64_out);
  nand nand_90 (nand_90_out, nand_41_out, nand_41_out);
  nand nand_91 (nand_91_out, nand_65_out, nand_66_out);
  nand nand_92 (nand_92_out, D0, D0);
  nand nand_93 (nand_93_out, nand_44_out, nand_67_out);
  nand nand_94 (nand_94_out, nand_68_out, nand_69_out);
  nand nand_95 (nand_95_out, nand_70_out, nand_70_out);
  nand nand_96 (nand_96_out, nand_71_out, nand_71_out);
  nand nand_97 (nand_97_out, nand_73_out, D0);
  nand nand_98 (nand_98_out, nand_99_out, nand_100_out);
  nand nand_99 (nand_99_out, nand_74_out, D2);
  nand nand_100 (nand_100_out, D3, nand_75_out);
  nand nand_101 (nand_101_out, nand_76_out, nand_77_out);
  nand nand_102 (nand_102_out, nand_78_out, nand_78_out);
  nand nand_103 (nand_103_out, nand_79_out, nand_79_out);
  nand nand_104 (nand_104_out, D0, D0);
  nand nand_105 (nand_105_out, nand_80_out, nand_80_out);
  nand nand_106 (nand_106_out, D0, D0);
  nand nand_107 (nand_107_out, nand_57_out, nand_84_out);
  nand nand_108 (nand_108_out, D0, D0);
  nand nand_109 (nand_109_out, D2, D2);
  nand nand_110 (nand_110_out, nand_85_out, nand_86_out);
  nand nand_111 (nand_111_out, nand_87_out, nand_88_out);
  nand nand_112 (nand_112_out, nand_90_out, D0);
  nand nand_113 (nand_113_out, nand_91_out, nand_91_out);
  nand nand_114 (nand_114_out, D3, nand_92_out);
  nand nand_115 (nand_115_out, nand_93_out, nand_93_out);
  nand nand_116 (nand_116_out, nand_95_out, D0);
  nand nand_117 (nand_117_out, nand_96_out, D0);
  nand nand_118 (nand_118_out, nand_72_out, nand_97_out);
  nand nand_119 (nand_119_out, nand_98_out, nand_98_out);
  nand nand_120 (nand_120_out, nand_101_out, nand_101_out);
  nand nand_121 (nand_121_out, nand_102_out, D0);
  nand nand_122 (nand_122_out, nand_103_out, nand_104_out);
  nand nand_123 (nand_123_out, nand_105_out, nand_106_out);
  nand nand_124 (nand_124_out, nand_107_out, nand_107_out);
  nand nand_125 (nand_125_out, nand_124_out, nand_126_out);
  nand nand_126 (nand_126_out, D2, nand_108_out);
  nand nand_127 (nand_127_out, D3, nand_109_out);
  nand nand_128 (nand_128_out, D3, D1);
  nand nand_129 (nand_129_out, nand_110_out, nand_110_out);
  nand nand_130 (nand_130_out, nand_111_out, nand_111_out);
  nand nand_131 (nand_131_out, nand_89_out, nand_112_out);
  nand nand_132 (nand_132_out, nand_113_out, nand_114_out);
  nand nand_133 (nand_133_out, nand_115_out, nand_94_out);
  nand nand_134 (nand_134_out, nand_116_out, nand_117_out);
  nand nand_135 (nand_135_out, nand_118_out, nand_118_out);
  nand nand_136 (nand_136_out, nand_120_out, nand_121_out);
  nand nand_137 (nand_137_out, nand_122_out, nand_123_out);
  nand nand_138 (nand_138_out, nand_125_out, nand_125_out);
  nand nand_139 (nand_139_out, nand_127_out, nand_128_out);
  nand nand_140 (g, nand_129_out, nand_130_out);
  nand nand_141 (nand_141_out, nand_131_out, nand_131_out);
  nand nand_142 (nand_142_out, nand_132_out, nand_132_out);
  nand nand_143 (nand_143_out, nand_133_out, nand_133_out);
  nand nand_144 (nand_144_out, nand_134_out, nand_134_out);
  nand nand_145 (c, nand_135_out, nand_119_out);
  nand nand_146 (nand_146_out, nand_136_out, nand_136_out);
  nand nand_147 (nand_147_out, nand_137_out, nand_137_out);
  nand nand_148 (nand_148_out, nand_139_out, nand_139_out);
  nand nand_149 (a, nand_141_out, nand_142_out);
  nand nand_150 (b, nand_143_out, nand_144_out);
  nand nand_151 (d, nand_146_out, nand_147_out);
  nand nand_152 (f, nand_138_out, nand_148_out);
endmodule

module contador9a0 (
  input  Q3,
  input  Q2,
  input  Q1,
  input  Q0,
  output D3,
  output D2,
  output D1,
  output D0
);

  wire and_1_out, and_2_out, and_3_out, and_4_out, and_5_out, and_6_out, and_7_out, and_8_out, not_1_out,
       not_2_out, not_3_out, not_4_out, not_5_out, not_6_out;

  not not_1 (not_1_out, Q1);
  not not_2 (not_2_out, Q0);
  not not_3 (not_3_out, Q3);
  not not_4 (not_4_out, Q2);
  not not_5 (not_5_out, Q1);
  not not_6 (not_6_out, Q0);
  and and_1 (and_1_out, Q3, Q0);
  and and_2 (and_2_out, not_3_out, not_4_out, not_5_out, not_6_out);
  and and_3 (and_3_out, Q0, Q2);
  and and_4 (and_4_out, Q2, Q1);
  and and_5 (and_5_out, Q3, not_2_out);
  and and_6 (and_6_out, Q2, not_1_out, not_2_out);
  and and_7 (and_7_out, not_2_out, Q3);
  and and_8 (and_8_out, Q1, Q0);
  or or_1 (D3, and_1_out, and_2_out);
  or or_2 (D2, and_3_out, and_4_out, and_5_out);
  or or_3 (D1, and_6_out, and_7_out, and_8_out);
  not not_7 (D0, Q0);
  Hex_Digit_Display hex_digit_display_1 (.value({D3, D2, D1, D0}));  // open: dp

  // Notes on the sheet:
  //   CONTADOR DE 9 A 0
endmodule

module contador5a0 (
  input  Q2,
  input  Q1,
  input  Q0,
  output out_4,
  output D1,
  output D0
);

  wire and_1_out, and_2_out, and_3_out, and_4_out, not_1_out, not_2_out, not_3_out;

  not not_1 (not_1_out, Q1);
  not not_2 (not_2_out, Q0);
  not not_3 (not_3_out, Q2);
  Hex_Digit_Display hex_digit_display_1 (.value({1'b0, out_4, D1, D0}));  // open: dp
  and and_1 (and_1_out, Q2, Q0);
  and and_2 (and_2_out, not_3_out, not_1_out, not_2_out);
  and and_3 (and_3_out, Q1, Q0);
  and and_4 (and_4_out, Q2, not_2_out);
  or or_1 (out_4, and_1_out, and_2_out);
  or or_2 (D1, and_3_out, and_4_out);
  not not_4 (D0, Q0);
endmodule
